// Logisim project Lecture02.circ as structural Verilog: 6 circuits, main circuit ALU
module ALU (
  input  [15:0] x,
  input  zx,
  input  nx,
  input  [15:0] y,
  input  zy,
  input  ny,
  input  f,
  input  no,
  output [15:0] out,
  output ng,
  output zr
);

  wire [15:0] add16_1_out, and_1_out, and_2_out, and_3_out, and_4_out, and_5_out, bit_extender_1_out,
       bit_extender_2_out, bit_extender_3_out, bit_extender_4_out, bit_extender_5_out, bit_extender_6_out,
       or_1_out, xor_1_out, xor_2_out;

  assign bit_extender_1_out = {{15{zx}}, zx};  // Bit_Extender bit_extender_1
  assign bit_extender_2_out = {{15{nx}}, nx};  // Bit_Extender bit_extender_2
  assign bit_extender_3_out = {{15{zy}}, zy};  // Bit_Extender bit_extender_3
  assign bit_extender_4_out = {{15{ny}}, ny};  // Bit_Extender bit_extender_4
  assign bit_extender_5_out = {{15{f}}, f};  // Bit_Extender bit_extender_5
  assign bit_extender_6_out = {{15{no}}, no};  // Bit_Extender bit_extender_6
  assign and_1_out = x & ~bit_extender_1_out;  // AND_Gate and_1, 16 bits wide
  assign and_2_out = y & ~bit_extender_3_out;  // AND_Gate and_2, 16 bits wide
  assign xor_1_out = and_1_out ^ bit_extender_2_out;  // XOR_Gate xor_1, 16 bits wide
  assign xor_2_out = and_2_out ^ bit_extender_4_out;  // XOR_Gate xor_2, 16 bits wide
  Add16 add16_1 (.a(xor_1_out), .b(xor_2_out), .out(add16_1_out));
  assign and_3_out = xor_1_out & xor_2_out;  // AND_Gate and_3, 16 bits wide
  assign and_4_out = add16_1_out & bit_extender_5_out;  // AND_Gate and_4, 16 bits wide
  assign and_5_out = ~bit_extender_5_out & and_3_out;  // AND_Gate and_5, 16 bits wide
  assign or_1_out = and_4_out | and_5_out;  // OR_Gate or_1, 16 bits wide
  assign out = or_1_out ^ bit_extender_6_out;  // XOR_Gate xor_3, 16 bits wide
  Comparator16 comparator16_1 (.ng(ng), .zr(zr), .in_1(out));

  // Notes on the sheet:
  //   w1
  //   w3
  //   w2
  //   w4
  //   and
  //   sum
  //   w5
  //   w6
  //   w7
  //   w8
endmodule

module Comparator16 (
  input  [15:0] in_1,
  output ng,
  output zr
);

  wire and_1_out, and_2_out, and_3_out, and_4_out, and_5_out, and_6_out, and_7_out, and_8_out, and_9_out,
       and_10_out, and_11_out, and_12_out, and_13_out, and_14_out;
  wire [15:0] not_1_out;

  and and_1 (and_1_out, not_1_out[15], not_1_out[14]);
  and and_2 (and_2_out, not_1_out[13], not_1_out[12]);
  assign not_1_out = ~in_1;  // NOT_Gate not_1, 16 bits wide
  and and_3 (and_3_out, not_1_out[9], not_1_out[8]);
  and and_4 (and_4_out, not_1_out[11], not_1_out[10]);
  and and_5 (and_5_out, not_1_out[3], not_1_out[2]);
  and and_6 (and_6_out, not_1_out[7], not_1_out[6]);
  and and_7 (and_7_out, not_1_out[5], not_1_out[4]);
  and and_8 (and_8_out, not_1_out[1], not_1_out[0]);
  and and_9 (and_9_out, and_8_out, and_5_out);
  and and_10 (and_10_out, and_7_out, and_6_out);
  and and_11 (and_11_out, and_3_out, and_4_out);
  and and_12 (and_12_out, and_2_out, and_1_out);
  and and_13 (and_13_out, and_9_out, and_10_out);
  and and_14 (and_14_out, and_11_out, and_12_out);
  and and_15 (zr, and_13_out, and_14_out);

  assign ng = in_1[15];
endmodule

module Inc16 (
  input  [15:0] in,
  output [15:0] out
);

  Add16 add16_1 (.a(in), .b(16'h1), .out(out));
endmodule

module Add16 (
  input  [15:0] a,
  input  [15:0] b,
  output [15:0] out
);

  wire fulladder_1_carry, fulladder_2_carry, fulladder_3_carry, fulladder_4_carry, fulladder_5_carry,
       fulladder_6_carry, fulladder_7_carry, fulladder_8_carry, fulladder_9_carry, fulladder_10_carry,
       fulladder_11_carry, fulladder_12_carry, fulladder_13_carry, fulladder_14_carry, halfadder_1_carry;

  HalfAdder halfadder_1 (.a(a[0]), .b(b[0]), .sum(out[0]), .carry(halfadder_1_carry));
  FullAdder fulladder_1 (.a(a[1]), .b(b[1]), .c(halfadder_1_carry), .carry(fulladder_1_carry), .sum(out[1]));
  FullAdder fulladder_2 (.a(a[2]), .b(b[2]), .c(fulladder_1_carry), .carry(fulladder_2_carry), .sum(out[2]));
  FullAdder fulladder_3 (.a(a[3]), .b(b[3]), .c(fulladder_2_carry), .carry(fulladder_3_carry), .sum(out[3]));
  FullAdder fulladder_4 (.a(a[4]), .b(b[4]), .c(fulladder_3_carry), .carry(fulladder_4_carry), .sum(out[4]));
  FullAdder fulladder_5 (.a(a[5]), .b(b[5]), .c(fulladder_4_carry), .carry(fulladder_5_carry), .sum(out[5]));
  FullAdder fulladder_6 (.a(a[6]), .b(b[6]), .c(fulladder_5_carry), .carry(fulladder_6_carry), .sum(out[6]));
  FullAdder fulladder_7 (.a(a[7]), .b(b[7]), .c(fulladder_6_carry), .carry(fulladder_7_carry), .sum(out[7]));
  FullAdder fulladder_8 (.a(a[8]), .b(b[8]), .c(fulladder_7_carry), .carry(fulladder_8_carry), .sum(out[8]));
  FullAdder fulladder_9 (.a(a[9]), .b(b[9]), .c(fulladder_8_carry), .carry(fulladder_9_carry), .sum(out[9]));
  FullAdder fulladder_10 (.a(a[10]), .b(b[10]), .c(fulladder_9_carry), .carry(fulladder_10_carry), .sum(out[10]));
  FullAdder fulladder_11 (.a(a[11]), .b(b[11]), .c(fulladder_10_carry), .carry(fulladder_11_carry), .sum(out[11]));
  FullAdder fulladder_12 (.a(a[12]), .b(b[12]), .c(fulladder_11_carry), .carry(fulladder_12_carry), .sum(out[12]));
  FullAdder fulladder_13 (.a(a[13]), .b(b[13]), .c(fulladder_12_carry), .carry(fulladder_13_carry), .sum(out[13]));
  FullAdder fulladder_14 (.a(a[14]), .b(b[14]), .c(fulladder_13_carry), .carry(fulladder_14_carry), .sum(out[14]));
  FullAdder fulladder_15 (.a(a[15]), .b(b[15]), .c(fulladder_14_carry), .sum(out[15]));  // open: carry

  // Other names for the same wires on the sheet: a00 = a[0]; a01 = a[1]; a02 = a[2]; a03 = a[3]; a04 = a[4];
  //   a05 = a[5]; a06 = a[6]; a07 = a[7]; a08 = a[8]; a09 = a[9]; b00 = b[0]; b01 = b[1]; b02 = b[2]; b03 = b[3];
  //   b04 = b[4]; b05 = b[5]; b06 = b[6]; b07 = b[7]; b08 = b[8]; b09 = b[9]
endmodule

module FullAdder (
  input  a,
  input  b,
  input  c,
  output carry,
  output sum
);

  wire halfadder_1_carry, halfadder_1_sum, halfadder_2_carry;

  HalfAdder halfadder_1 (.a(a), .b(b), .sum(halfadder_1_sum), .carry(halfadder_1_carry));
  HalfAdder halfadder_2 (.a(halfadder_1_sum), .b(c), .sum(sum), .carry(halfadder_2_carry));
  HalfAdder halfadder_3 (.a(halfadder_1_carry), .b(halfadder_2_carry), .sum(carry));  // open: carry
endmodule

module HalfAdder (
  input  a,
  input  b,
  output sum,
  output carry
);

  xor xor_1 (sum, a, b);
  and and_1 (carry, a, b);
endmodule
