// Logisim project MyComputer.circ as structural Verilog: 6 circuits, main circuit ALU
module ALU (
  input  [15:0] x,
  input  zx,
  input  nx,
  input  [15:0] y,
  input  zy,
  input  ny,
  input  f,
  input  no,
  output [15:0] out,
  output ng,
  output zr
);

  wire [15:0] adder_1_out, and_1_out, and_2_out, and_3_out, and_4_out, and_5_out, bit_extender_1_out,
       bit_extender_2_out, bit_extender_3_out, bit_extender_4_out, bit_extender_5_out, bit_extender_6_out,
       or_1_out, xor_1_out, xor_2_out;

  assign bit_extender_1_out = {{15{zx}}, zx};  // Bit_Extender bit_extender_1
  assign bit_extender_2_out = {{15{nx}}, nx};  // Bit_Extender bit_extender_2
  assign bit_extender_3_out = {{15{zy}}, zy};  // Bit_Extender bit_extender_3
  assign bit_extender_4_out = {{15{ny}}, ny};  // Bit_Extender bit_extender_4
  assign bit_extender_5_out = {{15{f}}, f};  // Bit_Extender bit_extender_5
  assign bit_extender_6_out = {{15{no}}, no};  // Bit_Extender bit_extender_6
  assign and_1_out = x & ~bit_extender_1_out;  // AND_Gate and_1, 16 bits wide
  assign and_2_out = y & ~bit_extender_3_out;  // AND_Gate and_2, 16 bits wide
  assign xor_1_out = and_1_out ^ bit_extender_2_out;  // XOR_Gate xor_1, 16 bits wide
  assign xor_2_out = and_2_out ^ bit_extender_4_out;  // XOR_Gate xor_2, 16 bits wide
  Adder #(.width(16)) adder_1 (.a(xor_1_out), .b(xor_2_out), .out(adder_1_out));  // open: cin, cout
  assign and_3_out = xor_1_out & xor_2_out;  // AND_Gate and_3, 16 bits wide
  assign and_4_out = adder_1_out & bit_extender_5_out;  // AND_Gate and_4, 16 bits wide
  assign and_5_out = ~bit_extender_5_out & and_3_out;  // AND_Gate and_5, 16 bits wide
  assign or_1_out = and_4_out | and_5_out;  // OR_Gate or_1, 16 bits wide
  assign out = or_1_out ^ bit_extender_6_out;  // XOR_Gate xor_3, 16 bits wide
  Comparator16 comparator16_1 (.ng(ng), .zr(zr), .in_1(out));

  // Notes on the sheet:
  //   w1
  //   w3
  //   w2
  //   w4
  //   and
  //   sum
  //   w5
  //   w6
  //   w7
  //   w8
endmodule

module Comparator16 (
  input  [15:0] in_1,
  output ng,
  output zr
);

  wire and_1_out, and_2_out, and_3_out, and_4_out, and_5_out, and_6_out, and_7_out, and_8_out, and_9_out,
       and_10_out, and_11_out, and_12_out, and_13_out, and_14_out;
  wire [15:0] not_1_out;

  and and_1 (and_1_out, not_1_out[15], not_1_out[14]);
  and and_2 (and_2_out, not_1_out[13], not_1_out[12]);
  assign not_1_out = ~in_1;  // NOT_Gate not_1, 16 bits wide
  and and_3 (and_3_out, not_1_out[9], not_1_out[8]);
  and and_4 (and_4_out, not_1_out[11], not_1_out[10]);
  and and_5 (and_5_out, not_1_out[7], not_1_out[6]);
  and and_6 (and_6_out, not_1_out[5], not_1_out[4]);
  and and_7 (and_7_out, not_1_out[3], not_1_out[2]);
  and and_8 (and_8_out, not_1_out[1], not_1_out[0]);
  and and_9 (and_9_out, and_8_out, and_7_out);
  and and_10 (and_10_out, and_6_out, and_5_out);
  and and_11 (and_11_out, and_3_out, and_4_out);
  and and_12 (and_12_out, and_2_out, and_1_out);
  and and_13 (and_13_out, and_9_out, and_10_out);
  and and_14 (and_14_out, and_11_out, and_12_out);
  and and_15 (zr, and_13_out, and_14_out);

  assign ng = in_1[15];
endmodule

module _1_Bit_Register (
  input  load,
  input  clock,
  input  in,
  output out
);

  wire multiplexer_1_out;

  Multiplexer #(.enable("false")) multiplexer_1 (.in0(out), .in1(in), .out(multiplexer_1_out), .sel(load));
  D_Flip_Flop d_ff_1 (.clk(clock), .D(multiplexer_1_out), .Q(out));  // open: Qn, preset, en, reset
endmodule

module Register (
  input  load,
  input  [15:0] in_2,
  input  clock,
  output [15:0] out_4
);

  _1_Bit_Register u_1_bit_register_1 (.in(in_2[0]), .out(out_4[0]), .load(load), .clock(clock));
  _1_Bit_Register u_1_bit_register_2 (.in(in_2[1]), .out(out_4[1]), .load(load), .clock(clock));
  _1_Bit_Register u_1_bit_register_3 (.in(in_2[2]), .out(out_4[2]), .load(load), .clock(clock));
  _1_Bit_Register u_1_bit_register_4 (.in(in_2[3]), .out(out_4[3]), .load(load), .clock(clock));
  _1_Bit_Register u_1_bit_register_5 (.in(in_2[4]), .out(out_4[4]), .load(load), .clock(clock));
  _1_Bit_Register u_1_bit_register_6 (.in(in_2[5]), .out(out_4[5]), .load(load), .clock(clock));
  _1_Bit_Register u_1_bit_register_7 (.in(in_2[6]), .out(out_4[6]), .load(load), .clock(clock));
  _1_Bit_Register u_1_bit_register_8 (.in(in_2[7]), .out(out_4[7]), .load(load), .clock(clock));
  _1_Bit_Register u_1_bit_register_9 (.in(in_2[8]), .out(out_4[8]), .load(load), .clock(clock));
  _1_Bit_Register u_1_bit_register_10 (.in(in_2[9]), .out(out_4[9]), .load(load), .clock(clock));
  _1_Bit_Register u_1_bit_register_11 (.in(in_2[10]), .out(out_4[10]), .load(load), .clock(clock));
  _1_Bit_Register u_1_bit_register_12 (.in(in_2[11]), .out(out_4[11]), .load(load), .clock(clock));
  _1_Bit_Register u_1_bit_register_13 (.in(in_2[12]), .out(out_4[12]), .load(load), .clock(clock));
  _1_Bit_Register u_1_bit_register_14 (.in(in_2[13]), .out(out_4[13]), .load(load), .clock(clock));
  _1_Bit_Register u_1_bit_register_15 (.in(in_2[14]), .out(out_4[14]), .load(load), .clock(clock));
  _1_Bit_Register u_1_bit_register_16 (.in(in_2[15]), .out(out_4[15]), .load(load), .clock(clock));
endmodule

module RAM8 (
  input  [15:0] in,
  input  load,
  input  [2:0] address,
  input  clock,
  output [15:0] out
);

  wire demultiplexer_1_out0, demultiplexer_1_out1, demultiplexer_1_out2, demultiplexer_1_out3,
       demultiplexer_1_out4, demultiplexer_1_out5, demultiplexer_1_out6, demultiplexer_1_out7;
  wire [15:0] register_1_out_4, register_2_out_4, register_3_out_4, register_4_out_4, register_5_out_4,
       register_6_out_4, register_7_out_4, register_8_out_4;

  Demultiplexer #(.select(3), .enable("false")) demultiplexer_1 (
    .out0(demultiplexer_1_out0), .out1(demultiplexer_1_out1), .out2(demultiplexer_1_out2),
    .out3(demultiplexer_1_out3), .out4(demultiplexer_1_out4), .out5(demultiplexer_1_out5),
    .out6(demultiplexer_1_out6), .out7(demultiplexer_1_out7), .in(load), .sel(address));
  Register register_1 (.load(demultiplexer_1_out0), .in_2(in), .clock(clock), .out_4(register_1_out_4));
  Register register_2 (.load(demultiplexer_1_out1), .in_2(in), .clock(clock), .out_4(register_2_out_4));
  Register register_3 (.load(demultiplexer_1_out2), .in_2(in), .clock(clock), .out_4(register_3_out_4));
  Register register_4 (.load(demultiplexer_1_out3), .in_2(in), .clock(clock), .out_4(register_4_out_4));
  Register register_5 (.load(demultiplexer_1_out4), .in_2(in), .clock(clock), .out_4(register_5_out_4));
  Register register_6 (.load(demultiplexer_1_out5), .in_2(in), .clock(clock), .out_4(register_6_out_4));
  Register register_7 (.load(demultiplexer_1_out6), .in_2(in), .clock(clock), .out_4(register_7_out_4));
  Register register_8 (.load(demultiplexer_1_out7), .in_2(in), .clock(clock), .out_4(register_8_out_4));
  Multiplexer #(.select(3), .width(16), .enable("false")) multiplexer_1 (
    .in0(register_1_out_4), .in1(register_2_out_4), .in2(register_3_out_4), .in3(register_4_out_4),
    .in4(register_5_out_4), .in5(register_6_out_4), .in6(register_7_out_4), .in7(register_8_out_4),
    .out(out), .sel(address));
endmodule

module RAM64 (
  input  [15:0] in,
  input  load,
  input  [5:0] address,
  input  clock,
  output [15:0] out
);

  wire demultiplexer_1_out0, demultiplexer_1_out1, demultiplexer_1_out2, demultiplexer_1_out3,
       demultiplexer_1_out4, demultiplexer_1_out5, demultiplexer_1_out6, demultiplexer_1_out7;
  wire [15:0] ram8_1_out, ram8_2_out, ram8_3_out, ram8_4_out, ram8_5_out, ram8_6_out, ram8_7_out, ram8_8_out;

  Demultiplexer #(.select(3), .enable("false")) demultiplexer_1 (
    .out0(demultiplexer_1_out0), .out1(demultiplexer_1_out1), .out2(demultiplexer_1_out2),
    .out3(demultiplexer_1_out3), .out4(demultiplexer_1_out4), .out5(demultiplexer_1_out5),
    .out6(demultiplexer_1_out6), .out7(demultiplexer_1_out7), .in(load), .sel(address[5:3]));
  RAM8 ram8_1 (.in(in), .load(demultiplexer_1_out0), .address(address[2:0]), .out(ram8_1_out), .clock(clock));
  RAM8 ram8_2 (.in(in), .load(demultiplexer_1_out1), .address(address[2:0]), .out(ram8_2_out), .clock(clock));
  RAM8 ram8_3 (.in(in), .load(demultiplexer_1_out2), .address(address[2:0]), .out(ram8_3_out), .clock(clock));
  RAM8 ram8_4 (.in(in), .load(demultiplexer_1_out3), .address(address[2:0]), .out(ram8_4_out), .clock(clock));
  RAM8 ram8_5 (.in(in), .load(demultiplexer_1_out4), .address(address[2:0]), .out(ram8_5_out), .clock(clock));
  RAM8 ram8_6 (.in(in), .load(demultiplexer_1_out5), .address(address[2:0]), .out(ram8_6_out), .clock(clock));
  RAM8 ram8_7 (.in(in), .load(demultiplexer_1_out6), .address(address[2:0]), .out(ram8_7_out), .clock(clock));
  RAM8 ram8_8 (.in(in), .load(demultiplexer_1_out7), .address(address[2:0]), .out(ram8_8_out), .clock(clock));
  Multiplexer #(.select(3), .width(16), .enable("false")) multiplexer_1 (
    .in0(ram8_1_out), .in1(ram8_2_out), .in2(ram8_3_out), .in3(ram8_4_out), .in4(ram8_5_out),
    .in5(ram8_6_out), .in6(ram8_7_out), .in7(ram8_8_out), .out(out), .sel(address[5:3]));
endmodule
